# Fritzing sketch circuit diagram (saved by Fritzing 0.9.5d)
breadboards: 1

parts:
  U1 = ESP8266 WiFi Module [part_number=ESP8266]
  부품1 = Arduino Uno (Rev3)
  R1 = Resistor [tolerance=±5% resistance=1k package="0805 [SMD]"]
  Mod1 = KY-004 Key Switch Module [package="Breakout board"]
  Mod2 = KY-012 Active Buzzer Module [package="Breakout board"]
  부품2 = SPI OLED Monochrome 128x64 0.96 inch
  R2 = Resistor [tolerance=±5% resistance=1k package="0805 [SMD]"]
  R3 = Resistor [tolerance=±5% resistance=1k package="0805 [SMD]"]
  Mod3 = KY-016 RGB Full Color LED Module [package="Breakout board"]

nets:
  N1: U1.RXD, R2.Pin_1, R3.Pin_0
  VCC: U1.VCC, U1.CH_PD, 부품1.3V3
  GND: U1.GND, 부품1.GND, R1.Pin_0, Mod1.-, Mod2.-, 부품2.GND, Mod3.-
  N2: U1.TXD, 부품1.D2
  N3: 부품1.D8, Mod1.S
  N4: 부품1.D9_PWM, 부품2.DC
  N5: 부품1.D10_PWM/SS, 부품2.CS
  N6: 부품1.D11_PWM/MOSI, 부품2.SDA
  N7: 부품1.D13/SCK, 부품2.SCK
  N8: 부품1.D3_PWM, R3.Pin_1
  N9: 부품1.D4, Mod3.R
  N10: 부품1.D5_PWM, Mod3.G
  N11: 부품1.D6_PWM, Mod3.B
  N12: 부품1.D7, Mod2.S
  N13: 부품1.RESET, 부품2.RES
  5V: 부품1.5V, Mod1.Vin, 부품2.VDD

custom parts:
  ESP8266 WiFi Module: Generic WiFi Module based on the ESP8266 with onboard PCB antenna and UART communications
  KY-004 Key Switch Module: Arduino Key Switch Module Keyes KY-004 is a push button that will output a high signal when pressed.
  KY-012 Active Buzzer Module: Active Piezoelectric Buzzer Module KY-012, it produces single-tone sound when signal is high. (Special thanks to vanepp for fixing the PCB holes and other errors)
  SPI OLED Monochrome 128x64 0.96 inch: Unknown 128x64 0.96 inch 128x64 SPI Monochrome OLED display
  KY-016 RGB Full Color LED Module: KY-016 Arduino full color 5mm RGB LED, different colors can be obtained by mixing the three primary colors.
